# Fritzing sketch schematic (saved by Fritzing 1.0.6)

parts:
  A1 = USB power module
  M1 = RioRand LM2596
  MCU1 = Raspberry Pi Zero
  Компонент1 = Thermal Printer

nets:
  N1: A1.Pin_1, A1.Pin_2, A1.Pin_3, M1.Pin_1, Компонент1.VH
  N2: A1.Pin_5, A1.Pin_6, M1.Pin_2, Компонент1.GND#0
  N3: M1.Pin_3, MCU1.pin_2, MCU1.pin_4
  N4: M1.Pin_4, MCU1.pin_6, MCU1.pin_14, Компонент1.GND#2
  N5: MCU1.pin_8, Компонент1.RXD
  N6: MCU1.pin_10, Компонент1.TXD

custom parts:
  USB power module: PD QC AFC Fast Charge Decoy Trigger Module USB-PWR Module Supports 5V 9V 12V 15V 20V Fixed Voltage Output.
